// Logisim project final_project.circ as structural Verilog: 1 circuit, main circuit main
module main (
);

  wire _0_out, _1_out, _2_out, _3_out, _4_out, _5_out, _6_out, _7_out, _8_out, _9_out, and_1_out, and_2_out,
       and_3_out, and_4_out, and_5_out, and_6_out, and_7_out, and_8_out, and_9_out, and_10_out, and_11_out,
       and_12_out, and_13_out, and_14_out, and_15_out, and_16_out, and_17_out, and_18_out, and_19_out,
       button_1_out, button_2_out, button_3_out, button_4_out, clock_1_out, clock_2_out, clock_3_out,
       clock_4_out, clock_5_out, comparator_1_eq, comparator_2_eq, comparator_3_eq, comparator_4_eq,
       comparator_5_eq, comparator_6_eq, comparator_7_eq, comparator_8_eq, d_ff_1_q, d_ff_2_q, d_ff_3_q,
       d_ff_4_q, d_ff_4_qn, d_ff_5_q, d_ff_5_qn, d_ff_6_q, d_ff_7_q, d_ff_8_q, d_ff_9_q, d_ff_9_qn,
       d_ff_10_q, d_ff_11_q, d_ff_12_q, d_ff_13_q, d_ff_14_q, d_ff_15_q, d_ff_16_q, d_ff_17_q, d_ff_17_qn,
       d_ff_18_q, d_ff_18_qn, d_ff_19_q, d_ff_20_q, d_ff_21_q, d_ff_22_q, d_ff_23_q, d_ff_23_qn, d_ff_24_q,
       d_ff_25_q, d_ff_25_qn, decoder_1_out1, decoder_1_out2, decoder_1_out3, decoder_1_out4, decoder_1_out5,
       decoder_2_out1, decoder_2_out2, decoder_2_out3, decoder_2_out4, decoder_2_out5, multiplexer_1_out,
       multiplexer_2_out, multiplexer_3_out, multiplexer_4_out, nor_1_out, not_1_out, not_2_out, not_3_out,
       not_4_out, not_5_out, not_6_out, not_7_out, not_8_out, or_1_out, or_2_out, or_3_out, or_4_out,
       or_5_out, or_6_out, or_7_out, or_8_out, or_9_out, or_10_out, or_11_out, or_12_out, or_13_out,
       or_14_out, or_15_out, or_16_out, or_17_out, priority_encoder_1_gs, register_13_q, register_14_q,
       register_15_q, register_16_q, shift_register_1_q0, shift_register_1_q11, shift_register_2_q11,
       shift_register_3_q11, shift_register_4_out, shift_register_4_q0, shift_register_5_out,
       shift_register_6_out, shift_register_6_q0, shift_register_6_q5, shift_register_7_q0,
       shift_register_7_q1, shift_register_7_q2, shift_register_7_q3, shift_register_8_out,
       shift_register_8_q0, undriven;
  wire [1:0] counter_4_q;
  wire [2:0] counter_1_q, counter_2_q, counter_3_q;
  wire [3:0] priority_encoder_1_out, register_1_q, register_2_q, register_3_q, register_4_q, register_5_q,
       register_6_q, register_7_q, register_8_q, register_9_q, register_10_q, register_11_q, register_12_q,
       rom_1_data, rom_2_data, rom_3_data, rom_4_data, transistor_1_out, transistor_2_out, transistor_3_out,
       transistor_4_out;

  Clock clock_1 (.out(clock_1_out));
  D_Flip_Flop d_ff_1 (.clk(clock_1_out), .D(d_ff_5_qn), .Q(d_ff_1_q));  // open: Qn, preset, en, reset
  or or_1 (or_1_out, d_ff_3_q, or_7_out);
  D_Flip_Flop d_ff_2 (.clk(clock_1_out), .D(d_ff_1_q), .Q(d_ff_2_q));  // open: Qn, preset, en, reset
  D_Flip_Flop d_ff_3 (
    .clk(counter_3_q[2]), .D(counter_3_q[2]), .Q(d_ff_3_q), .reset(d_ff_4_q));  // open: Qn, preset, en
  D_Flip_Flop d_ff_4 (.clk(d_ff_5_q), .D(or_1_out), .Q(d_ff_4_q), .Qn(d_ff_4_qn));  // open: preset, en, reset
  or or_2 (or_2_out, d_ff_4_q, d_ff_3_q);
  LED led_1 (.in(or_2_out));
  D_Flip_Flop d_ff_5 (.clk(clock_1_out), .D(d_ff_2_q), .Q(d_ff_5_q), .Qn(d_ff_5_qn));  // open: preset, en, reset
  and and_1 (and_1_out, counter_3_q[1], counter_3_q[0]);
  or or_3 (or_3_out, d_ff_4_q, d_ff_3_q, and_1_out);
  or or_4 (or_4_out, d_ff_4_q, d_ff_3_q, counter_3_q[1]);
  LED led_2 (.in(or_3_out));
  LED led_3 (.in(or_4_out));
  or or_5 (or_5_out, counter_3_q[1], counter_3_q[0]);
  or or_6 (or_6_out, d_ff_4_q, d_ff_3_q, or_5_out);
  LED led_4 (.in(or_6_out));
  D_Flip_Flop d_ff_6 (
    .clk(and_2_out), .D(and_2_out), .Q(d_ff_6_q), .reset(shift_register_1_q0));  // open: Qn, preset, en
  LED led_5 (.in(and_14_out));
  LED led_6 (.in(shift_register_4_out));
  Button button_1 (.out(button_1_out));
  Button button_2 (.out(button_2_out));
  Button _0 (.out(_0_out));
  Button _1 (.out(_1_out));
  Button _2 (.out(_2_out));
  Button _3 (.out(_3_out));
  Button _4 (.out(_4_out));
  Button _5 (.out(_5_out));
  Button _6 (.out(_6_out));
  Button _7 (.out(_7_out));
  Button _8 (.out(_8_out));
  Button _9 (.out(_9_out));
  Button button_3 (.out(button_3_out));
  LED led_7 (.in(and_19_out));
  Shift_Register #(.length(12)) shift_register_1 (
    .in(d_ff_6_q), .clk(d_ff_23_q), .clr(or_9_out), .q0(shift_register_1_q0), .q11(shift_register_1_q11));  // open: shift, out, load, d0, d1, q1, d2, q2, d3, q3, d4, q4, d5, q5, d6, q6, d7, q7, d8, q8, d9, q9, d10, q10, d11
  Shift_Register #(.length(12)) shift_register_2 (
    .in(shift_register_1_q11), .clk(d_ff_23_q), .clr(or_9_out), .q11(shift_register_2_q11));  // open: shift, out, load, d0, q0, d1, q1, d2, q2, d3, q3, d4, q4, d5, q5, d6, q6, d7, q7, d8, q8, d9, q9, d10, q10, d11
  Shift_Register #(.length(12)) shift_register_3 (
    .in(shift_register_2_q11), .clk(d_ff_23_q), .clr(or_9_out), .q11(shift_register_3_q11));  // open: shift, out, load, d0, q0, d1, q1, d2, q2, d3, q3, d4, q4, d5, q5, d6, q6, d7, q7, d8, q8, d9, q9, d10, q10, d11
  or or_7 (or_7_out, counter_2_q[2], and_4_out);
  or or_8 (or_8_out, and_7_out, and_5_out);
  and and_2 (and_2_out, d_ff_12_q, button_1_out);
  and and_3 (and_3_out, button_2_out, or_13_out);
  D_Flip_Flop d_ff_7 (
    .clk(and_13_out), .D(and_13_out), .Q(d_ff_7_q), .reset(shift_register_4_q0));  // open: Qn, preset, en
  Shift_Register #(.length(3)) shift_register_4 (
    .in(1'b0), .clk(d_ff_23_q), .out(shift_register_4_out), .load(d_ff_7_q), .d0(d_ff_7_q),
    .q0(shift_register_4_q0), .d1(d_ff_7_q), .d2(d_ff_7_q));  // open: shift, clr, q1, q2
  and and_4 (and_4_out, counter_1_q[2], ~d_ff_9_q);  // AND_Gate
  D_Flip_Flop d_ff_8 (.clk(and_2_out), .D(and_2_out), .Q(d_ff_8_q), .reset(or_9_out));  // open: Qn, preset, en
  D_Flip_Flop d_ff_9 (
    .clk(and_3_out), .D(and_3_out), .Q(d_ff_9_q), .Qn(d_ff_9_qn), .reset(or_9_out));  // open: preset, en
  or or_9 (or_9_out, and_12_out, shift_register_3_q11, button_3_out);
  Priority_Encoder #(.select(4)) priority_encoder_1 (
    .in0(_0_out), .in1(_1_out), .in2(_2_out), .in3(_3_out), .in4(_4_out), .in5(_5_out), .in6(_6_out),
    .in7(_7_out), .in8(_8_out), .in9(_9_out), .out(priority_encoder_1_out), .gs(priority_encoder_1_gs));  // open: in10, in11, in12, in13, in14, in15, en_out, en_in
  not not_1 (not_1_out, and_19_out);
  Counter #(.width(3), .max('h7)) counter_1 (
    .Q(counter_1_q), .clk(and_5_out), .clr(or_9_out));  // open: load, D, count, carry
  and and_5 (and_5_out, priority_encoder_1_gs, ~decoder_1_out5, d_ff_8_q);  // AND_Gate
  and and_6 (and_6_out, button_3_out, not_1_out);
  Decoder #(.select(3)) decoder_1 (
    .out1(decoder_1_out1), .out2(decoder_1_out2), .out3(decoder_1_out3), .out4(decoder_1_out4),
    .out5(decoder_1_out5), .sel(counter_1_q));  // open: out0, out6, out7, en
  and and_7 (and_7_out, d_ff_9_q, priority_encoder_1_gs, ~decoder_2_out5, d_ff_8_q);  // AND_Gate
  not not_2 (not_2_out, and_13_out);
  Transistor #(.gate("br"), .width(4)) transistor_1 (.in(register_5_q), .out(transistor_1_out), .gate(not_2_out));
  Clock clock_2 (.out(clock_2_out));
  or or_10 (or_10_out, or_8_out, and_8_out);
  and and_8 (and_8_out, ~d_ff_8_q, and_9_out);  // AND_Gate
  and and_9 (and_9_out, ~d_ff_8_q, not_1_out, priority_encoder_1_gs);  // AND_Gate
  Register #(.width(4)) register_1 (
    .D(priority_encoder_1_out), .en(d_ff_9_qn), .Q(register_1_q), .clk(decoder_1_out1));  // open: clr
  Counter #(.width(3), .max('h7)) counter_2 (
    .Q(counter_2_q), .clk(and_7_out), .clr(or_9_out));  // open: load, D, count, carry
  Counter #(.width(3), .max('h7)) counter_3 (
    .Q(counter_3_q), .clk(or_10_out), .clr(or_11_out));  // open: load, D, count, carry
  or or_11 (or_11_out, counter_3_q[2], and_3_out, or_9_out, and_10_out);
  and and_10 (and_10_out, or_12_out, ~d_ff_8_q);  // AND_Gate
  or or_12 (or_12_out, and_6_out, shift_register_6_q5);
  or or_13 (or_13_out, decoder_1_out5, decoder_1_out4);
  Register #(.width(4)) register_2 (
    .D(priority_encoder_1_out), .en(d_ff_9_qn), .Q(register_2_q), .clk(decoder_1_out2));  // open: clr
  Decoder #(.select(3)) decoder_2 (
    .out1(decoder_2_out1), .out2(decoder_2_out2), .out3(decoder_2_out3), .out4(decoder_2_out4),
    .out5(decoder_2_out5), .sel(counter_2_q));  // open: out0, out6, out7, en
  not not_3 (not_3_out, and_13_out);
  ROM #(.addrWidth(4), .dataWidth(4)) rom_1 (.addr(transistor_1_out), .data(rom_1_data));  // open: sel
  Transistor #(.gate("br"), .width(4)) transistor_2 (.in(register_7_q), .out(transistor_2_out), .gate(not_3_out));
  Register #(.width(4)) register_3 (.D(rom_1_data), .Q(register_3_q), .clk(clock_2_out));  // open: en, clr
  Counter #(.width(2), .max('h3)) counter_4 (
    .Q(counter_4_q), .clk(and_9_out), .clr(or_12_out));  // open: load, D, count, carry
  Register #(.width(4)) register_4 (
    .D(priority_encoder_1_out), .en(d_ff_9_qn), .Q(register_4_q), .clk(decoder_1_out3));  // open: clr
  or or_14 (or_14_out, decoder_2_out5, decoder_2_out4);
  Register #(.width(4)) register_5 (
    .D(priority_encoder_1_out), .en(d_ff_9_q), .Q(register_5_q), .clk(decoder_2_out1));  // open: clr
  Comparator #(.width(1)) comparator_1 (
    .a(multiplexer_4_out), .b(priority_encoder_1_out[0]), .eq(comparator_1_eq));  // open: gt, lt
  Comparator #(.width(1)) comparator_2 (
    .a(multiplexer_3_out), .b(priority_encoder_1_out[1]), .eq(comparator_2_eq));  // open: gt, lt
  Comparator #(.width(1)) comparator_3 (
    .a(multiplexer_2_out), .b(priority_encoder_1_out[2]), .eq(comparator_3_eq));  // open: gt, lt
  Comparator #(.width(1)) comparator_4 (
    .a(multiplexer_1_out), .b(priority_encoder_1_out[3]), .eq(comparator_4_eq));  // open: gt, lt
  Register #(.width(4)) register_6 (
    .D(priority_encoder_1_out), .en(d_ff_9_qn), .Q(register_6_q), .clk(decoder_1_out4));  // open: clr
  Register #(.width(4)) register_7 (
    .D(priority_encoder_1_out), .en(d_ff_9_q), .Q(register_7_q), .clk(decoder_2_out2));  // open: clr
  Register #(.width(4)) register_8 (
    .D(priority_encoder_1_out), .en(d_ff_9_q), .Q(register_8_q), .clk(decoder_2_out3));  // open: clr
  ROM #(.addrWidth(4), .dataWidth(4)) rom_2 (.addr(transistor_2_out), .data(rom_2_data));  // open: sel
  Multiplexer #(.select(2), .enable("false")) multiplexer_1 (
    .in0(register_12_q[3]), .in1(register_3_q[3]), .in2(register_10_q[3]), .in3(register_11_q[3]),
    .out(multiplexer_1_out), .sel(counter_4_q));
  and and_11 (and_11_out, comparator_1_eq, comparator_2_eq, priority_encoder_1_gs, comparator_3_eq, comparator_4_eq);
  Register #(.width(4)) register_9 (
    .D(priority_encoder_1_out), .en(d_ff_9_q), .Q(register_9_q), .clk(decoder_2_out4));  // open: clr
  not not_4 (not_4_out, and_13_out);
  Transistor #(.gate("br"), .width(4)) transistor_3 (.in(register_8_q), .out(transistor_3_out), .gate(not_4_out));
  Register #(.width(4)) register_10 (.D(rom_2_data), .Q(register_10_q), .clk(clock_2_out));  // open: en, clr
  and and_12 (and_12_out, and_3_out, or_14_out);
  Multiplexer #(.select(2), .enable("false")) multiplexer_2 (
    .in0(register_12_q[2]), .in1(register_3_q[2]), .in2(register_10_q[2]), .in3(register_11_q[2]),
    .out(multiplexer_2_out), .sel(counter_4_q));
  not not_5 (not_5_out, and_13_out);
  Transistor #(.gate("br"), .width(4)) transistor_4 (.in(register_9_q), .out(transistor_4_out), .gate(not_5_out));
  ROM #(.addrWidth(4), .dataWidth(4)) rom_3 (.addr(transistor_3_out), .data(rom_3_data));  // open: sel
  Multiplexer #(.select(2), .enable("false")) multiplexer_3 (
    .in0(register_12_q[1]), .in1(register_3_q[1]), .in2(register_10_q[1]), .in3(register_11_q[1]),
    .out(multiplexer_3_out), .sel(counter_4_q));
  Comparator #(.width(4)) comparator_5 (.a(register_1_q), .b(register_5_q), .eq(comparator_5_eq));  // open: gt, lt
  Comparator #(.width(4)) comparator_6 (.a(register_2_q), .b(register_7_q), .eq(comparator_6_eq));  // open: gt, lt
  Comparator #(.width(4)) comparator_7 (.a(register_4_q), .b(register_8_q), .eq(comparator_7_eq));  // open: gt, lt
  Comparator #(.width(4)) comparator_8 (.a(register_6_q), .b(register_9_q), .eq(comparator_8_eq));  // open: gt, lt
  Register #(.width(4)) register_11 (.D(rom_3_data), .Q(register_11_q), .clk(clock_2_out));  // open: en, clr
  and and_13 (and_13_out, comparator_5_eq, comparator_6_eq, and_12_out, comparator_7_eq, comparator_8_eq);
  ROM #(.addrWidth(4), .dataWidth(4)) rom_4 (.addr(transistor_4_out), .data(rom_4_data));  // open: sel
  Multiplexer #(.select(2), .enable("false")) multiplexer_4 (
    .in0(register_12_q[0]), .in1(register_3_q[0]), .in2(register_10_q[0]), .in3(register_11_q[0]),
    .out(multiplexer_4_out), .sel(counter_4_q));
  Clock clock_3 (.out(clock_3_out));
  Register #(.width(4)) register_12 (.D(rom_4_data), .Q(register_12_q), .clk(clock_2_out));  // open: en, clr
  D_Flip_Flop d_ff_10 (.clk(d_ff_18_q), .D(d_ff_17_qn), .Q(d_ff_10_q));  // open: Qn, preset, en, reset
  D_Flip_Flop d_ff_11 (.clk(clock_3_out), .D(d_ff_18_qn), .Q(d_ff_11_q));  // open: Qn, preset, en, reset
  D_Flip_Flop d_ff_12 (.clk(and_18_out), .D(and_18_out), .Q(d_ff_12_q), .reset(and_14_out));  // open: Qn, preset, en
  and and_14 (and_14_out, not_7_out, or_16_out);
  not not_6 (not_6_out, counter_4_q[1]);
  D_Flip_Flop d_ff_13 (
    .clk(d_ff_18_q), .D(d_ff_10_q), .Q(d_ff_13_q), .en(undriven), .reset(undriven));  // open: Qn, preset
  D_Flip_Flop d_ff_14 (.clk(clock_3_out), .D(d_ff_11_q), .Q(d_ff_14_q));  // open: Qn, preset, en, reset
  not not_7 (not_7_out, and_19_out);
  and and_15 (and_15_out, counter_4_q[0], not_6_out);
  D_Flip_Flop d_ff_15 (.clk(d_ff_18_q), .D(d_ff_13_q), .Q(d_ff_15_q));  // open: Qn, preset, en, reset
  D_Flip_Flop d_ff_16 (.clk(clock_3_out), .D(d_ff_14_q), .Q(d_ff_16_q));  // open: Qn, preset, en, reset
  Clock clock_4 (.out(clock_4_out));
  or or_15 (or_15_out, and_6_out, nor_1_out);
  Clock clock_5 (.out(clock_5_out));
  Register #(.width(1)) register_13 (
    .D(and_15_out), .Q(register_13_q), .clk(and_15_out), .clr(shift_register_6_q0));  // open: en
  D_Flip_Flop d_ff_17 (.clk(d_ff_18_q), .D(d_ff_15_q), .Q(d_ff_17_q), .Qn(d_ff_17_qn));  // open: preset, en, reset
  D_Flip_Flop d_ff_18 (.clk(clock_3_out), .D(d_ff_16_q), .Q(d_ff_18_q), .Qn(d_ff_18_qn));  // open: preset, en, reset
  D_Flip_Flop d_ff_19 (.clk(clock_4_out), .D(d_ff_25_qn), .Q(d_ff_19_q));  // open: Qn, preset, en, reset
  D_Flip_Flop d_ff_20 (.Q(d_ff_20_q), .preset(and_11_out), .reset(and_16_out));  // open: clk, D, Qn, en
  and and_16 (and_16_out, and_9_out, ~and_11_out);  // AND_Gate
  nor nor_1 (nor_1_out, counter_4_q[1], counter_4_q[0]);
  Shift_Register #(.length(2)) shift_register_5 (
    .in(or_15_out), .clk(clock_5_out), .out(shift_register_5_out), .clr(and_9_out));  // open: shift, load, d0, q0, d1, q1
  Shift_Register #(.length(6)) shift_register_6 (
    .in(register_13_q), .clk(d_ff_17_q), .out(shift_register_6_out), .clr(or_15_out),
    .q0(shift_register_6_q0), .q5(shift_register_6_q5));  // open: shift, load, d0, d1, q1, d2, q2, d3, q3, d4, q4, d5
  Register #(.width(1)) register_14 (
    .D(and_15_out), .Q(register_14_q), .clk(and_15_out), .clr(shift_register_6_out));  // open: en
  D_Flip_Flop d_ff_21 (.clk(d_ff_25_q), .D(d_ff_23_qn), .Q(d_ff_21_q));  // open: Qn, preset, en, reset
  D_Flip_Flop d_ff_22 (.clk(clock_4_out), .D(d_ff_19_q), .Q(d_ff_22_q));  // open: Qn, preset, en, reset
  Shift_Register #(.length(4), .trigger("falling")) shift_register_7 (
    .in(d_ff_20_q), .clk(and_9_out), .clr(or_16_out), .q0(shift_register_7_q0), .q1(shift_register_7_q1),
    .q2(shift_register_7_q2), .q3(shift_register_7_q3));  // open: shift, out, load, d0, d1, d2, d3
  or or_16 (or_16_out, shift_register_5_out, and_17_out);
  and and_17 (and_17_out, shift_register_6_out, register_14_q);
  D_Flip_Flop d_ff_23 (.clk(d_ff_25_q), .D(d_ff_21_q), .Q(d_ff_23_q), .Qn(d_ff_23_qn));  // open: preset, en, reset
  D_Flip_Flop d_ff_24 (.clk(clock_4_out), .D(d_ff_22_q), .Q(d_ff_24_q));  // open: Qn, preset, en, reset
  Button button_4 (.out(button_4_out));
  D_Flip_Flop d_ff_25 (.clk(clock_4_out), .D(d_ff_24_q), .Q(d_ff_25_q), .Qn(d_ff_25_qn));  // open: preset, en, reset
  and and_18 (and_18_out, shift_register_7_q3, shift_register_7_q2, shift_register_7_q1, shift_register_7_q0);
  or or_17 (or_17_out, button_4_out, and_18_out);
  Register #(.width(1)) register_15 (
    .D(or_17_out), .Q(register_15_q), .clk(or_17_out), .clr(shift_register_8_q0));  // open: en
  Shift_Register #(.length(5)) shift_register_8 (
    .in(register_15_q), .clk(d_ff_23_q), .out(shift_register_8_out), .q0(shift_register_8_q0));  // open: shift, load, clr, d0, d1, q1, d2, q2, d3, q3, d4, q4
  Register #(.width(1)) register_16 (
    .D(or_17_out), .Q(register_16_q), .clk(or_17_out), .clr(shift_register_8_out));  // open: en
  not not_8 (not_8_out, shift_register_8_out);
  and and_19 (and_19_out, not_8_out, register_16_q);
  LED led_8 (.in(and_19_out));

  // Notes on the sheet:
  //   Keypad
  //   Door Closed
  //   Change Password
  //   OK
  //   Reset
  //   Door Open
  //   36 seconds
  //   contents of rom_1 (hex, n*v repeats v):
  //   0 1 2 3 4 5 6 7 8 9
  //   contents of rom_2 (hex, n*v repeats v):
  //   0 1 2 3 4 5 6 7 8 9
  //   Left bit
  //   contents of rom_3 (hex, n*v repeats v):
  //   0 1 2 3 4 5 6 7 8 9
  //   ORDER IN EVERY MUX: 4° number - 1° number- 2° number - 3° number
  //   contents of rom_4 (hex, n*v repeats v):
  //   0 1 2 3 4 5 6 7 8 9
  //   Right Bit
  //   Frequency 1Hz
  //   Frequency 2Hz
  //   Frequency 64Hz
  //   Time 0s
  //   Time 11s
  //   Clear of Shift Register
  //   Inside Button
  //   Time 4.5s
  //   Lock
endmodule
